// Logisim project calculator.circ as structural Verilog: 1 circuit, main circuit main
module main (
);

  wire adder_1_cout, adder_1_out, adder_2_cout, adder_2_out, adder_3_cout, adder_3_out, adder_4_cout,
       adder_4_out, adder_5_cout, adder_5_out, adder_6_cout, adder_6_out, adder_7_cout, adder_7_out,
       adder_8_cout, adder_8_out, adder_9_cout, adder_9_out, adder_10_cout, adder_10_out, adder_11_cout,
       adder_11_out, adder_12_cout, adder_12_out, adder_13_cout, adder_13_out, adder_14_cout, adder_14_out,
       adder_15_cout, adder_15_out, adder_16_cout, adder_16_out, and_1_out, and_2_out, and_3_out, and_4_out,
       and_5_out, and_6_out, and_7_out, and_8_out, and_9_out, and_10_out, and_11_out, and_12_out, and_13_out,
       and_14_out, and_15_out, and_16_out, multiplexer_1_out, multiplexer_2_out, multiplexer_3_out,
       multiplexer_4_out, multiplexer_5_out, multiplexer_6_out, multiplexer_7_out, multiplexer_8_out,
       xor_1_out, xor_2_out, xor_3_out, xor_4_out;

  xor xor_1 (xor_1_out, 1'b0, 1'b0);
  and and_1 (and_1_out, 1'b1, 1'b0);
  and and_2 (and_2_out, 1'b0, 1'b1);
  and and_3 (and_3_out, 1'b0, 1'b1);
  and and_4 (and_4_out, 1'b0, 1'b1);
  Adder #(.width(1)) adder_1 (.a(and_2_out), .b(and_5_out), .out(adder_1_out), .cout(adder_1_cout));  // open: cin
  Adder #(.width(1)) adder_2 (.a(and_3_out), .b(and_6_out), .out(adder_2_out), .cin(adder_1_cout), .cout(adder_2_cout));
  Adder #(.width(1)) adder_3 (.a(and_4_out), .b(and_7_out), .out(adder_3_out), .cin(adder_2_cout), .cout(adder_3_cout));
  Adder #(.width(1)) adder_4 (.a(1'b0), .b(and_8_out), .out(adder_4_out), .cin(adder_3_cout), .cout(adder_4_cout));
  xor xor_2 (xor_2_out, 1'b0, 1'b1);
  and and_5 (and_5_out, 1'b1, 1'b1);
  and and_6 (and_6_out, 1'b1, 1'b1);
  and and_7 (and_7_out, 1'b1, 1'b1);
  and and_8 (and_8_out, 1'b1, 1'b1);
  Adder #(.width(1)) adder_5 (.a(adder_2_out), .b(and_9_out), .out(adder_5_out), .cin(1'b0), .cout(adder_5_cout));
  Adder #(.width(1)) adder_6 (
    .a(adder_3_out), .b(and_10_out), .out(adder_6_out), .cin(adder_5_cout), .cout(adder_6_cout));
  Adder #(.width(1)) adder_7 (
    .a(adder_4_out), .b(and_11_out), .out(adder_7_out), .cin(adder_6_cout), .cout(adder_7_cout));
  Adder #(.width(1)) adder_8 (
    .a(and_12_out), .b(adder_4_cout), .out(adder_8_out), .cin(adder_7_cout), .cout(adder_8_cout));
  xor xor_3 (xor_3_out, 1'b0, 1'b1);
  and and_9 (and_9_out, 1'b1, 1'b1);
  and and_10 (and_10_out, 1'b1, 1'b1);
  and and_11 (and_11_out, 1'b1, 1'b1);
  and and_12 (and_12_out, 1'b1, 1'b1);
  and and_13 (and_13_out, 1'b1, 1'b1);
  and and_14 (and_14_out, 1'b1, 1'b1);
  and and_15 (and_15_out, 1'b1, 1'b1);
  and and_16 (and_16_out, 1'b1, 1'b1);
  xor xor_4 (xor_4_out, 1'b0, 1'b1);
  Adder #(.width(1)) adder_9 (.a(and_13_out), .b(adder_6_out), .out(adder_9_out), .cin(1'b0), .cout(adder_9_cout));
  Adder #(.width(1)) adder_10 (
    .a(and_14_out), .b(adder_7_out), .out(adder_10_out), .cin(adder_9_cout), .cout(adder_10_cout));
  Adder #(.width(1)) adder_11 (
    .a(and_15_out), .b(adder_8_out), .out(adder_11_out), .cin(adder_10_cout), .cout(adder_11_cout));
  Adder #(.width(1)) adder_12 (
    .a(adder_8_cout), .b(and_16_out), .out(adder_12_out), .cin(adder_11_cout), .cout(adder_12_cout));
  Adder #(.width(1)) adder_13 (.a(1'b1), .b(xor_1_out), .out(adder_13_out), .cin(1'b0), .cout(adder_13_cout));
  Adder #(.width(1)) adder_14 (.a(1'b1), .b(xor_2_out), .out(adder_14_out), .cin(adder_13_cout), .cout(adder_14_cout));
  Adder #(.width(1)) adder_15 (.a(1'b1), .b(xor_3_out), .out(adder_15_out), .cin(adder_14_cout), .cout(adder_15_cout));
  Adder #(.width(1)) adder_16 (.a(1'b1), .b(xor_4_out), .out(adder_16_out), .cin(adder_15_cout), .cout(adder_16_cout));
  Multiplexer #(.select(2), .enable("false")) multiplexer_1 (
    .in0(adder_13_out), .in1(and_1_out), .in2(adder_13_out), .out(multiplexer_1_out), .sel(2'b00));  // open: in3
  Multiplexer #(.select(2), .enable("false")) multiplexer_2 (
    .in0(adder_14_out), .in1(adder_1_out), .in2(adder_14_out), .out(multiplexer_2_out), .sel(2'b00));  // open: in3
  Multiplexer #(.select(2), .enable("false")) multiplexer_3 (
    .in0(adder_15_out), .in1(adder_5_out), .in2(adder_15_out), .out(multiplexer_3_out), .sel(2'b00));  // open: in3
  Multiplexer #(.select(2), .enable("false")) multiplexer_4 (
    .in0(adder_16_out), .in1(adder_9_out), .in2(adder_16_out), .out(multiplexer_4_out), .sel(2'b00));  // open: in3
  Multiplexer #(.select(2), .enable("false")) multiplexer_5 (
    .in0(adder_16_cout), .in1(adder_10_out), .in2(adder_16_cout), .out(multiplexer_5_out), .sel(2'b00));  // open: in3
  Multiplexer #(.select(2), .enable("false")) multiplexer_6 (
    .in1(adder_11_out), .out(multiplexer_6_out), .sel(2'b00));  // open: in0, in2, in3
  Multiplexer #(.select(2), .enable("false")) multiplexer_7 (
    .in1(adder_12_out), .out(multiplexer_7_out), .sel(2'b00));  // open: in0, in2, in3
  Multiplexer #(.select(2), .enable("false")) multiplexer_8 (
    .in1(adder_12_cout), .out(multiplexer_8_out), .sel(2'b00));  // open: in0, in2, in3
  LED led_1 (.in(multiplexer_1_out));
  LED led_2 (.in(multiplexer_2_out));
  LED led_3 (.in(multiplexer_3_out));
  LED led_4 (.in(multiplexer_4_out));
  LED led_5 (.in(multiplexer_5_out));
  LED led_6 (.in(multiplexer_6_out));
  LED led_7 (.in(multiplexer_7_out));
  LED led_8 (.in(multiplexer_8_out));

  // Notes on the sheet:
  //   A0
  //   B0
  //   A1
  //   B1
  //   A2
  //   B2
  //   A3
  //   B3
  //   k
  //   o0
  //   o1
  //   o2
  //   o3
  //   o4
  //   o5
  //   o6
  //   o7
endmodule
